// Logisim project CONTADOR CRESCENTE 4BIT COM RESET.circ as structural Verilog: 1 circuit, main circuit main
module main (
  input  in_1,
  input  in_2,
  input  in_3,
  input  in_4,
  input  in_5,
  input  in_6,
  output Q0,
  output Q1,
  output Q2,
  output Q2_2
);

  wire and_1_out, and_2_out, and_3_out, or_1_out;

  J_K_Flip_Flop j_k_ff_1 (
    .J(1'b1), .clk(in_5), .K(1'b1), .Q(Q0), .preset(in_1), .en(1'b1), .reset(or_1_out));  // open: Qn
  or or_1 (or_1_out, in_6, and_1_out);
  and and_1 (and_1_out, Q1, Q2_2);
  J_K_Flip_Flop j_k_ff_2 (.J(Q0), .clk(in_5), .K(Q0), .Q(Q1), .preset(in_2), .en(1'b1), .reset(or_1_out));  // open: Qn
  and and_2 (and_2_out, Q0, Q1);
  J_K_Flip_Flop j_k_ff_3 (
    .J(and_2_out), .clk(in_5), .K(and_2_out), .Q(Q2), .preset(in_3), .en(1'b1), .reset(or_1_out));  // open: Qn
  and and_3 (and_3_out, and_2_out, Q2);
  J_K_Flip_Flop j_k_ff_4 (
    .J(and_3_out), .clk(in_5), .K(and_3_out), .Q(Q2_2), .preset(in_4), .en(1'b1), .reset(or_1_out));  // open: Qn
endmodule
