// Logisim project CONTADOR CRESCENTE 4BIT.circ as structural Verilog: 1 circuit, main circuit main
module main (
  input  in_1,
  input  in_2,
  input  in_3,
  input  in_4,
  input  in_5,
  input  in_6,
  input  in_7,
  input  in_8,
  input  in_9,
  output Q0,
  output Q1,
  output Q2,
  output Q2_2
);

  wire and_1_out, and_2_out;

  J_K_Flip_Flop j_k_ff_1 (.J(1'b1), .clk(in_9), .K(1'b1), .Q(Q0), .preset(in_1), .en(1'b1), .reset(in_2));  // open: Qn
  J_K_Flip_Flop j_k_ff_2 (.J(Q0), .clk(in_9), .K(Q0), .Q(Q1), .preset(in_3), .en(1'b1), .reset(in_4));  // open: Qn
  and and_1 (and_1_out, Q0, Q1);
  J_K_Flip_Flop j_k_ff_3 (
    .J(and_1_out), .clk(in_9), .K(and_1_out), .Q(Q2), .preset(in_5), .en(1'b1), .reset(in_6));  // open: Qn
  and and_2 (and_2_out, and_1_out, Q2);
  J_K_Flip_Flop j_k_ff_4 (
    .J(and_2_out), .clk(in_9), .K(and_2_out), .Q(Q2_2), .preset(in_7), .en(1'b1), .reset(in_8));  // open: Qn

  // Notes on the sheet:
  //   CONTADOR CRESCENTE 4BIT
endmodule
