// Logisim project contador-cresccente-4bits-auto.circ as structural Verilog: 1 circuit, main circuit main
module main (
);

  wire clock_1_out, main_1_p2, main_1_p3, main_1_p4, main_1_p5;

  LED led_1 (.in(main_1_p2));
  Clock clock_1 (.out(clock_1_out));
  LED led_2 (.in(main_1_p5));
  LED led_3 (.in(main_1_p3));
  LED led_4 (.in(main_1_p4));
  // contador_crescente_4bits_main main_1: pin names not known; wires that end beside it: clock_1_out, main_1_p2, main_1_p3, main_1_p4, main_1_p5

  // Notes on the sheet:
  //   Versão automatica do contador crescente
endmodule
