// Logisim project contador-crescente-4bits.circ as structural Verilog: 1 circuit, main circuit main
module main (
  input  in_1,
  output Q3,
  output Q2,
  output Q1,
  output Q0
);

  wire and_1_out, and_2_out;

  J_K_Flip_Flop j_k_ff_1 (.J(1'b1), .clk(in_1), .K(1'b1), .Q(Q0), .preset(1'b0), .en(1'b1), .reset(1'b0));  // open: Qn
  and and_1 (and_1_out, Q0, Q1);
  J_K_Flip_Flop j_k_ff_2 (.J(Q0), .clk(in_1), .K(Q0), .Q(Q1), .preset(1'b0), .en(1'b1), .reset(1'b0));  // open: Qn
  J_K_Flip_Flop j_k_ff_3 (
    .J(and_1_out), .clk(in_1), .K(and_1_out), .Q(Q2), .preset(1'b0), .en(1'b1), .reset(1'b0));  // open: Qn
  and and_2 (and_2_out, and_1_out, Q2);
  J_K_Flip_Flop j_k_ff_4 (
    .J(and_2_out), .clk(in_1), .K(and_2_out), .Q(Q3), .preset(1'b0), .en(1'b1), .reset(1'b0));  // open: Qn

  // Notes on the sheet:
  //   CONTADOR CRESCENTE DE 4BITS
endmodule
