// Logisim project contador-em-anel.circ as structural Verilog: 1 circuit, main circuit main
module main (
  input  in_1
);

  wire d_ff_1_q, d_ff_2_q, d_ff_3_q, d_ff_4_q;

  LED led_1 (.in(d_ff_1_q));
  D_Flip_Flop d_ff_1 (.clk(in_1), .D(d_ff_4_q), .Q(d_ff_1_q), .preset(1'b0), .en(1'b1), .reset(1'b0));  // open: Qn
  LED led_2 (.in(d_ff_2_q));
  D_Flip_Flop d_ff_2 (.clk(in_1), .D(d_ff_1_q), .Q(d_ff_2_q), .preset(1'b0), .en(1'b1), .reset(1'b0));  // open: Qn
  LED led_3 (.in(d_ff_3_q));
  D_Flip_Flop d_ff_3 (.clk(in_1), .D(d_ff_2_q), .Q(d_ff_3_q), .preset(1'b0), .en(1'b1), .reset(1'b0));  // open: Qn
  LED led_4 (.in(d_ff_4_q));
  D_Flip_Flop d_ff_4 (.clk(in_1), .D(d_ff_3_q), .Q(d_ff_4_q), .preset(1'b0), .en(1'b1), .reset(1'b0));  // open: Qn

  // Notes on the sheet:
  //   CONTADOR EM ANEL
endmodule
