// Logisim project 1_decodificador-7-seg.circ as structural Verilog: 1 circuit, main circuit main
module main (
  input  in_1
);

  wire clock_1_out, decifrador_completo_1_p5, decifrador_completo_1_p6, decifrador_completo_1_p7,
       decifrador_completo_1_p8, decifrador_completo_1_p9, decifrador_completo_1_p10,
       decifrador_completo_1_p11, main_1_p3, main_1_p4, main_1_p5, main_1_p6;

  Clock clock_1 (.out(clock_1_out));
  // CONTADOR_UP_DOWN_4BIT_main main_1: pin names not known; wires that end beside it: in_1, clock_1_out, main_1_p3, main_1_p4, main_1_p5, main_1_p6
  // decifrador_completo decifrador_completo_1: pin names not known; wires that end beside it: main_1_p6, main_1_p5, main_1_p4, main_1_p3, decifrador_completo_1_p5, decifrador_completo_1_p6, decifrador_completo_1_p7, decifrador_completo_1_p8, decifrador_completo_1_p9, decifrador_completo_1_p10, decifrador_completo_1_p11
  _7_Segment_Display u_7_segment_display_1 (
    .g(decifrador_completo_1_p11), .f(decifrador_completo_1_p10), .a(decifrador_completo_1_p5),
    .b(decifrador_completo_1_p6), .e(decifrador_completo_1_p9), .d(decifrador_completo_1_p8),
    .c(decifrador_completo_1_p7));  // open: dp
endmodule
