// Logisim project 3_contador-up-down-4bits.circ as structural Verilog: 1 circuit, main circuit main
module main (
  input  DOWN,
  input  in_2,
  output Q0,
  output Q1,
  output Q2,
  output Q3
);

  wire and_1_out, and_2_out, and_3_out, and_4_out, and_5_out, and_6_out, j_k_ff_1_qn, j_k_ff_2_qn,
       j_k_ff_3_qn, not_1_out, or_1_out, or_2_out, or_3_out;

  J_K_Flip_Flop j_k_ff_1 (
    .J(1'b1), .clk(in_2), .K(1'b1), .Q(Q0), .Qn(j_k_ff_1_qn), .preset(1'b0), .en(1'b1), .reset(1'b0));
  not not_1 (not_1_out, DOWN);
  and and_1 (and_1_out, DOWN, Q0);
  and and_2 (and_2_out, j_k_ff_1_qn, not_1_out);
  or or_1 (or_1_out, and_1_out, and_2_out);
  J_K_Flip_Flop j_k_ff_2 (
    .J(or_1_out), .clk(in_2), .K(or_1_out), .Q(Q1), .Qn(j_k_ff_2_qn), .preset(1'b0), .en(1'b1), .reset(1'b0));
  and and_3 (and_3_out, and_1_out, Q1);
  and and_4 (and_4_out, j_k_ff_2_qn, and_2_out);
  or or_2 (or_2_out, and_3_out, and_4_out);
  J_K_Flip_Flop j_k_ff_3 (
    .J(or_2_out), .clk(in_2), .K(or_2_out), .Q(Q2), .Qn(j_k_ff_3_qn), .preset(1'b0), .en(1'b1), .reset(1'b0));
  and and_5 (and_5_out, and_3_out, Q2);
  and and_6 (and_6_out, j_k_ff_3_qn, and_4_out);
  or or_3 (or_3_out, and_5_out, and_6_out);
  J_K_Flip_Flop j_k_ff_4 (
    .J(or_3_out), .clk(in_2), .K(or_3_out), .Q(Q3), .preset(1'b0), .en(1'b1), .reset(1'b0));  // open: Qn

  // Notes on the sheet:
  //   CONTADOR UP-DOWN 4BIT
endmodule
