// Logisim project CONTADOR_DECODIFICADOR_2.circ as structural Verilog: 1 circuit, main circuit main
module main (
  input  in_1
);

  wire and_1_out, clock_1_out, decifrador_completo_1_p5, decifrador_completo_1_p6, decifrador_completo_1_p7,
       decifrador_completo_1_p8, decifrador_completo_1_p9, decifrador_completo_1_p10,
       decifrador_completo_1_p11, decifrador_completo_2_p5, decifrador_completo_2_p6,
       decifrador_completo_2_p7, decifrador_completo_2_p8, decifrador_completo_2_p9,
       decifrador_completo_2_p10, decifrador_completo_2_p11, main_1_p3, main_1_p4, main_1_p5, main_1_p6,
       main_2_p3, main_2_p4, main_2_p5, main_2_p6, not_1_out, not_2_out;

  and and_1 (and_1_out, main_1_p3, not_1_out, not_2_out, main_1_p6);
  not not_1 (not_1_out, main_1_p4);
  not not_2 (not_2_out, main_1_p5);
  Clock clock_1 (.out(clock_1_out));
  // CONTADOR_UP_DOWN_4BIT_main main_1: pin names not known; wires that end beside it: in_1, clock_1_out, main_1_p3, main_1_p4, main_1_p5, main_1_p6
  // CONTADOR_UP_DOWN_4BIT_main main_2: pin names not known; wires that end beside it: in_1, and_1_out, main_2_p3, main_2_p4, main_2_p5, main_2_p6
  // decifrador_completo decifrador_completo_1: pin names not known; wires that end beside it: main_1_p6, main_1_p5, main_1_p4, main_1_p3, decifrador_completo_1_p5, decifrador_completo_1_p6, decifrador_completo_1_p7, decifrador_completo_1_p8, decifrador_completo_1_p9, decifrador_completo_1_p10, decifrador_completo_1_p11
  // decifrador_completo decifrador_completo_2: pin names not known; wires that end beside it: main_2_p6, main_2_p5, main_2_p4, main_2_p3, decifrador_completo_2_p5, decifrador_completo_2_p6, decifrador_completo_2_p7, decifrador_completo_2_p8, decifrador_completo_2_p9, decifrador_completo_2_p10, decifrador_completo_2_p11
  _7_Segment_Display u_7_segment_display_1 (
    .g(decifrador_completo_1_p11), .f(decifrador_completo_1_p10), .a(decifrador_completo_1_p5),
    .b(decifrador_completo_1_p6), .e(decifrador_completo_1_p9), .d(decifrador_completo_1_p8),
    .c(decifrador_completo_1_p7));  // open: dp
  _7_Segment_Display u_7_segment_display_2 (
    .g(decifrador_completo_2_p11), .f(decifrador_completo_2_p10), .a(decifrador_completo_2_p5),
    .b(decifrador_completo_2_p6), .e(decifrador_completo_2_p9), .d(decifrador_completo_2_p8),
    .c(decifrador_completo_2_p7));  // open: dp
endmodule
