// Logisim project decodificador-7seg-auto.circ as structural Verilog: 1 circuit, main circuit main
module main (
  input  in_1,
  input  in_2,
  input  in_3,
  input  in_4
);

  wire main_1_p5, main_1_p6, main_1_p7, main_1_p8, main_1_p9, main_1_p10, main_1_p11;

  // decodificador_7seg_main main_1: pin names not known; wires that end beside it: in_1, in_2, in_3, in_4, main_1_p5, main_1_p6, main_1_p7, main_1_p8, main_1_p9, main_1_p10, main_1_p11
  _7_Segment_Display u_7_segment_display_1 (
    .g(main_1_p11), .f(main_1_p10), .a(main_1_p5), .b(main_1_p6), .e(main_1_p9), .d(main_1_p8), .c(main_1_p7));  // open: dp
endmodule
