// Logisim project somador-positivo-4bits.circ as structural Verilog: 1 circuit, main circuit main
module main (
  input  a3,
  input  b3,
  input  a2,
  input  b2,
  input  a1,
  input  b1,
  input  a0,
  input  b0,
  input  vem_1,
  output vai_1,
  output r3,
  output r2,
  output r1,
  output r0
);

  wire main_1_p3, main_2_p3, main_3_p3;

  // macro1_main main_1: pin names not known; wires that end beside it: a3, b3, main_1_p3, r3, vai_1
  // macro1_main main_2: pin names not known; wires that end beside it: a2, b2, main_2_p3, r2, main_1_p3
  // macro1_main main_3: pin names not known; wires that end beside it: a1, b1, main_3_p3, r1, main_2_p3
  // macro1_main main_4: pin names not known; wires that end beside it: a0, b0, vem_1, r0, main_3_p3
endmodule
