// Logisim project primeiro-macro.circ as structural Verilog: 1 circuit, main circuit main
module main (
  input  a,
  input  b,
  input  vem_1,
  output r,
  output vai_1
);

  wire and_1_out, and_2_out, xor_1_out;

  xor xor_1 (xor_1_out, a, b);
  and and_1 (and_1_out, a, b);
  xor xor_2 (r, xor_1_out, vem_1);
  and and_2 (and_2_out, xor_1_out, vem_1);
  or or_1 (vai_1, and_2_out, and_1_out);
endmodule
